# Fritzing sketch button-no-continuity (saved by Fritzing 0.9.5d)
breadboards: 1

parts:
  R3 = Resistor [tolerance=±5% resistance=470 package="0603 [SMD]"]
  R4 = Resistor [tolerance=±5% resistance=10k package="0603 [SMD]"]
  S3 = Momentary Switch [package=ksa_sealed_tac_switch]
  M1 = Multimeter [package=multimeter]

nets:
  N1: R3.Pin_1, R4.Pin_0, S3.2, M1.COM
  N2: S3.4, M1.V-OHM

notes:
  GPIO input
  Continuity testing: there should *not* be continuity between these pins.

custom parts:
  Multimeter: Basic Multimeter for graphical demonstrations
