# Fritzing sketch pi-button (saved by Fritzing 0.9.5d)
breadboards: 1

parts:
  R3 = Resistor [tolerance=±5% resistance=470 package="0603 [SMD]"]
  R4 = Resistor [tolerance=±5% resistance=10k package="0603 [SMD]"]
  Raspberry_Pi_1 = Raspberry Pi Zero  # not connected
  MCU1 = Raspberry Pi Zero
  S3 = Momentary Switch [package=ksa_sealed_tac_switch]

nets:
  N1: R3.Pin_0, MCU1.pin_11
  N2: R3.Pin_1, R4.Pin_0, S3.2
  N3: R4.Pin_1, MCU1.pin_14, MCU1.pin_34
  N4: MCU1.pin_1, MCU1.pin_17, S3.4

notes:
  GPIO input
