# Fritzing sketch pi-led (saved by Fritzing 0.9.5d)
breadboards: 1

parts:
  R1 = Resistor [tolerance=±5% resistance=470 package="0603 [SMD]"]
  LED1 = LEDs [package=led10mm]
  MCU1 = Raspberry Pi Zero

nets:
  N1: R1.Pin_0, LED1.A
  N2: R1.Pin_1, MCU1.pin_11
  N3: LED1.C, MCU1.pin_6, MCU1.pin_9
