# Fritzing sketch breadboard-rgb (saved by Fritzing 0.9.5d)
breadboards: 1

parts:
  R3 = Resistor [tolerance=±5% resistance=470 package="0603 [SMD]"]
  LED1 = RGB LED (com. cathode, rgb) [package="5 mm [THT]"]
  R5 = Resistor [tolerance=±5% resistance=470 package="0603 [SMD]"]
  R6 = Resistor [tolerance=±5% resistance=470 package="0603 [SMD]"]
  MCU1 = Raspberry Pi Zero

nets:
  N1: R3.Pin_0, LED1.red_anode
  N2: R3.Pin_1, MCU1.pin_12
  N3: LED1.common_cathode, MCU1.pin_14, MCU1.pin_34
  N4: LED1.green_anode, R6.Pin_0
  N5: LED1.blue_anode, R5.Pin_0

notes:
  RGB LED pins:
  1. Red anode (to 470Ω)
  2. Common cathode (longest)
  3. Green anode (to 470Ω)
  4. Blue anode (to 470Ω)
