# Fritzing sketch parallel-lcd (saved by Fritzing 0.9.5d)
breadboards: 1

parts:
  U1 = LCD-16X2 [package=lcd-16x2]
  R1 = Resistor [tolerance=±5% resistance=220 package="0603 [SMD]"]
  MCU1 = Raspberry Pi Zero
  POT1 = Breadboard Trimpot

nets:
  N1: U1.VSS, U1.R_W, U1.K, MCU1.pin_6, MCU1.pin_39, POT1.PIN3
  N2: U1.VDD, R1.Pin_0, MCU1.pin_2, MCU1.pin_4, POT1.PIN1
  N3: U1.VO, POT1.PIN2
  N4: U1.RS, MCU1.pin_31
  N5: U1.E, MCU1.pin_29
  N6: U1.DB4, MCU1.pin_22
  N7: U1.DB5, MCU1.pin_18
  N8: U1.DB6, MCU1.pin_16
  N9: U1.DB7, MCU1.pin_15
  N10: U1.A, R1.Pin_1
