# Fritzing sketch pi-oled (saved by Fritzing 0.9.5d)
breadboards: 1

parts:
  OLED_I2C1 = OLED 128x64 I2C Monochrome Display
  MCU1 = Raspberry Pi Zero

nets:
  N1: OLED_I2C1.SDA, MCU1.pin_3
  N2: OLED_I2C1.SCK, MCU1.pin_5
  N3: OLED_I2C1.VDD, MCU1.pin_1, MCU1.pin_17
  N4: OLED_I2C1.GND, MCU1.pin_9, MCU1.pin_20

notes:
  Carefully read the labels printed next to the pins on your OLED - the order is not always the same!
  - GND to GND
  - VCC/VDD to 3.3V
  - SCL/SCK to GPIO3
  - SDA to GPIO2
