# Fritzing sketch pi-rfid (saved by Fritzing 0.9.5d)
breadboards: 1

parts:
  Raspberry_Pi_1 = Raspberry Pi 3 [part_number=RPI-3-V1.2]
  Part1 = RFID-RC522 [part_number=101218]

nets:
  GND: Raspberry_Pi_1.GND, Part1.GND
  3V3: Raspberry_Pi_1.3V3, Part1.3.3V
  N1: Raspberry_Pi_1.GPIO10, Part1.MOSI
  N2: Raspberry_Pi_1.GPIO9, Part1.MISO
  N3: Raspberry_Pi_1.GPIO11, Part1.SCK
  N4: Raspberry_Pi_1.GPIO8, Part1.SDA
  N5: Raspberry_Pi_1.GPIO25, Part1.RST

notes:
  Gray- GPIO8 to SDA (CE)
  Purple - GPIO11 to SCK (Clock)
  Blue - GPIO10 to MOSI
  Green - GPIO9 to MISO
  Black - GND to GND
  White - GPIO25 to RST
  Red - 3.3V to 3.3V
