# Fritzing sketch uart-hc05 (saved by Fritzing 0.9.5d)
breadboards: 1

parts:
  Part1 = Bluetooth HC-05 Macho
  MCU1 = Raspberry Pi Zero

nets:
  N1: Part1.State, MCU1.pin_16
  N2: Part1.TXD, MCU1.pin_10
  N3: Part1.RXD, MCU1.pin_8
  N4: Part1.VCC, MCU1.pin_1, MCU1.pin_17
  N5: Part1.Key, MCU1.pin_18
  N6: Part1.GND, MCU1.pin_6, MCU1.pin_39

notes:
  Note: on some HC-05 modules, the order of pins may be different!
