# Fritzing sketch buzzer (saved by Fritzing 0.9.5d)
breadboards: 1

parts:
  Q2 = TRANSISTOR_NPN [package=to-92]
  R1 = Resistor [tolerance=±5% resistance=220 package="2010 [SMD]"]
  buz1 = Piezo Buzzer
  R2 = Resistor [tolerance=±5% resistance=4.7k package="2010 [SMD]"]
  MCU1 = Raspberry Pi Zero

nets:
  N1: Q2.E, MCU1.pin_39
  N2: Q2.B, R2.Pin_1
  N3: Q2.C, R1.Pin_1
  N4: R1.Pin_0, buz1.pin_1
  N5: buz1.pin_2, MCU1.pin_2, MCU1.pin_4
  N6: R2.Pin_0, MCU1.pin_37

custom parts:
  Piezo Buzzer: Part from https://www.nutsvolts.com/magazine/article/november2012_SmileysWorkshop modified to be .3 in spacing to match the adafruit buzzer 5V breadboard friendly part.
