# Fritzing sketch logic-level (saved by Fritzing 0.9.5d)
breadboards: 1

parts:
  R4 = Resistor [tolerance=±5% resistance=10k package=THT]
  Q2 = 2N7000 FET N-Channel [part_number=2N7000 package=TO92]
  R3 = Resistor [tolerance=±5% resistance=10k package=THT]
  M1 = Multimeter [package=multimeter]
  MCU1 = Raspberry Pi Zero

nets:
  5V supply: R4.Pin_0, MCU1.pin_2, MCU1.pin_4
  5V I/O: R4.Pin_1, Q2.drain, M1.V-OHM
  3.3V logic (S)/3.3V supply: Q2.gate, Q2.source, R3.Pin_0, R3.Pin_1, MCU1.pin_1, MCU1.pin_17
  N1: M1.COM, MCU1.pin_34, MCU1.pin_39

notes:
  Test: 3.3V I/O line drives circuit HIGH:
  5V I/O line is "input" (measure on multimeter)

custom parts:
  2N7000 FET N-Channel: A 2N7000 MOSFET N-Channel Transistor
  Multimeter: Basic Multimeter for graphical demonstrations
