# Fritzing sketch pi-HC-SR04 (saved by Fritzing 0.9.3b)
breadboards: 1

parts:
  hc-sr2 = hc-sr04
  Raspberry_Pi_2 = Raspberry Pi 3 [part_number=RPI-3-V1.2]
  R3 = Resistor [tolerance=±5% resistance=2.2k package=THT]
  R4 = Resistor [tolerance=±5% resistance=1.2k package=THT]

nets:
  VCC: hc-sr2.VCC, Raspberry_Pi_2.5V
  N1: hc-sr2.Trig, Raspberry_Pi_2.GIPO14
  N2: hc-sr2.Echo, R4.Pin_0
  N3: Raspberry_Pi_2.GND, R3.Pin_1
  N4: Raspberry_Pi_2.GIPO23, R3.Pin_0, R4.Pin_1

notes:
  Trig -> GPIO14
  Echo -> Voltage divider -> GPIO23
