# Fritzing sketch shift-register-pi (saved by Fritzing 0.9.3b)
breadboards: 1

parts:
  U1 = 74HC595 [package="DIP16 [THT]"]
  R1 = Resistor [tolerance=±5% resistance=470 package="0402 [SMD]"]
  R2 = Resistor [tolerance=±5% resistance=470 package="0402 [SMD]"]
  R3 = Resistor [tolerance=±5% resistance=470 package="0402 [SMD]"]
  R4 = Resistor [tolerance=±5% resistance=470 package="0402 [SMD]"]
  R5 = Resistor [tolerance=±5% resistance=470 package="0402 [SMD]"]
  R6 = Resistor [tolerance=±5% resistance=470 package="0402 [SMD]"]
  R7 = Resistor [tolerance=±5% resistance=470 package="0402 [SMD]"]
  LED11 = LED - 3mm [color="Yellow (595nm)" package="3 mm [THT]"]
  LED12 = LED - 3mm [color="Yellow (595nm)" package="3 mm [THT]"]
  LED13 = LED - 3mm [color="Yellow (595nm)" package="3 mm [THT]"]
  LED14 = LED - 3mm [color="Yellow (595nm)" package="3 mm [THT]"]
  LED15 = LED - 3mm [color="Yellow (595nm)" package="3 mm [THT]"]
  LED16 = LED - 3mm [color="Yellow (595nm)" package="3 mm [THT]"]
  LED17 = LED - 3mm [color="Yellow (595nm)" package="3 mm [THT]"]
  LED18 = LED - 3mm [color="Yellow (595nm)" package="3 mm [THT]"]
  R8 = Resistor [tolerance=±5% resistance=470 package="0402 [SMD]"]
  Raspberry_Pi_1 = Raspberry Pi 3 [part_number=RPI-3-V1.2]

nets (from the breadboard view):
  N1: U1.Q1, R6.Pin_0
  N2: U1.Q2, R4.Pin_0
  N3: U1.Q3, R3.Pin_0
  N4: U1.Q4, R2.Pin_0
  N5: U1.Q5, R1.Pin_0
  N6: U1.Q6, R5.Pin_0
  N7: U1.Q7, R8.Pin_0
  GND: U1.GND, U1.OE, LED11.cathode, LED12.cathode, LED13.cathode, LED14.cathode, LED15.cathode, LED16.cathode, LED17.cathode, LED18.cathode, Raspberry_Pi_1.GND
  3V3: U1.MR, U1.VCC, Raspberry_Pi_1.3v3, Raspberry_Pi_1.3V3
  N8: U1.SH_CP, Raspberry_Pi_1.GIPO11
  N9: U1.ST_CP, Raspberry_Pi_1.GIPO8
  N10: U1.DS, Raspberry_Pi_1.GIPO10
  N11: U1.Q0, R7.Pin_0
  N12: R1.Pin_1, LED16.anode
  N13: R2.Pin_1, LED15.anode
  N14: R3.Pin_1, LED14.anode
  N15: R4.Pin_1, LED13.anode
  N16: R5.Pin_1, LED17.anode
  N17: R6.Pin_1, LED12.anode
  N18: R7.Pin_1, LED11.anode
  N19: LED18.anode, R8.Pin_1

notes:
  Green: DS (serial input) to BCM 10
  Orange: ST_CP/RCLK to BCM 8
  Purple: SH_CP/SRCLK to BCM11
